# Fritzing sketch robot (saved by Fritzing 1.0.7)
breadboards: 1

parts:
  Mod1 = Raspberry Pi Pico W
  Mod2 = L298N DC motor driver
  M1 = DC Motor [voltage_(max)=6V voltage_(min)=3V]
  VCC1 = Battery [internal_resistance=0.1Ω]
  M2 = DC Motor [voltage_(max)=6V voltage_(min)=3V]
  Mod3 = L298N DC motor driver
  M3 = DC Motor [voltage_(max)=6V voltage_(min)=3V]
  M4 = DC Motor [voltage_(max)=6V voltage_(min)=3V]
  R1 = Resistor [tolerance=±5% power=0.25W resistance=15 package=THT]
  LED2 = LED - 5mm [color="Green (565nm)" current=0.030A package="5 mm [THT]"]
  LED3 = LED - 5mm [color="Red (633nm)" current=0.030A package="5 mm [THT]"]
  R2 = Resistor [tolerance=±5% power=0.25W resistance=150 package=THT]

nets:
  GND: Mod1.pin_3, Mod1.pin_8, Mod1.pin_13, Mod1.pin_18, Mod1.pin_23, Mod1.pin_28, Mod1.pin_33, Mod1.pin_38, Mod1.pin_42, Mod2.GND, VCC1.-, Mod3.GND, LED2.cathode, LED3.cathode
  N1: Mod1.pin_4, Mod2.ENB
  N2: Mod1.pin_5, Mod2.IN4
  N3: Mod1.pin_6, Mod2.IN3
  N4: Mod1.pin_7, Mod2.IN2
  N5: Mod1.pin_9, Mod2.IN1
  N6: Mod1.pin_10, Mod2.ENA
  N7: Mod1.pin_19, R2.Pin_0
  N8: Mod1.pin_20, R1.Pin_0
  N9: Mod1.pin_24, Mod3.ENB
  N10: Mod1.pin_25, Mod3.IN4
  N11: Mod1.pin_26, Mod3.IN3
  N12: Mod1.pin_27, Mod3.IN2
  N13: Mod1.pin_29, Mod3.IN1
  N14: Mod1.pin_31, Mod3.ENA
  N15: Mod1.pin_39, Mod3.5V, Mod3.+5V-J1
  N16: Mod2.OUT1, M1.pin_2
  N17: Mod2.OUT2, M1.pin_1
  12V: Mod2.12V, VCC1.+, Mod3.12V
  N18: Mod2.OUT3, M2.pin_2
  N19: Mod2.OUT4, M2.pin_1
  N20: Mod3.OUT1, M3.pin_2
  N21: Mod3.OUT2, M3.pin_1
  N22: Mod3.OUT3, M4.pin_2
  N23: Mod3.OUT4, M4.pin_1
  N24: R1.Pin_1, LED2.anode
  N25: LED3.anode, R2.Pin_1

custom parts:
  Raspberry Pi Pico W: Raspberry Pi Pico W. Based around the RP2040 microcontroller the Pico W is a low cost microcontroller device bringing Raspberry Pi quality, cost, and easy of use to the microcontroller space. The areas marked KEEPOUT in pcb silkscreen should not have traces running through them to avoid shorts on a soldered in module!
  L298N DC motor driver: 2x DC motor driver with 78M05 positive voltage regulator (7..35 V) L298N: max 46 V, 2 A Set 5 V Enable jumper to enable 5 V regultor (needed for the L298N) and +5 V output at screw terminal or supply external +5 V at screw terminal Set ENA and/or ENB to +5 V to enable motor permanently or supply ENA and/or ENB with PWM signal IN1 and IN2 set rotation directory for motor A (OUT1/OUT2) IN2 and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
